// Logisim project 4bitAdder.circ as structural Verilog: 4 circuits, main circuit main
// Number Correct
module main (
  input  Enable_Halt
);

  wire and_2_out, CLK, Correct, Halt, not_1_out, not_2_out, NotDone, YourCout;
  wire [3:0] A, B, YourSum;
  wire [4:0] Solution;
  wire [8:0] Number_Correct_q;

  not not_1 (not_1_out, Correct);
  and and_1 (Halt, Enable_Halt, not_1_out);
  Clock clock_1 (.out(CLK));
  Inputs inputs_1 (.Halt(Halt), .Clk(CLK), .A(A), .B(B), .NotDone(NotDone));
  // Probe on A
  // Probe on B
  // Probe on YourSum
  // Probe on YourCout
  // Probe on Solution[3:0]
  // Probe on Solution[4]
  _4bitAdder _4BitAdder (.A(A), .B(B), .Cin(1'b0), .Sum(YourSum), .Cout(YourCout));
  not not_2 (not_2_out, Halt);
  and and_2 (and_2_out, Correct, NotDone, not_2_out);
  Checker checker_1 (.A(A), .B(B), .Sum(YourSum), .Cout(YourCout), .Correct(Correct), .CorrectAnswer(Solution));
  Counter #(.width(9), .max('h100)) Number_Correct (
    .count(and_2_out), .Q(Number_Correct_q), .clk(CLK));  // open: load, D, carry, clr
  // Probe on Number_Correct_q

  // Notes on the sheet:
  //   Guoqin Sun & Kun Xiao
  //   914785301 & 914696908
endmodule

module _4bitAdder (
  input  [3:0] A,
  input  [3:0] B,
  input  Cin,
  output [3:0] Sum,
  output Cout
);

  wire and_5_out, and_6_out, and_7_out, and_8_out, and_9_out, and_10_out, and_11_out, and_12_out, and_13_out,
       and_14_out, C0, C1, C2, G0, G1, G2, G3, P0, P1, P2, P3;

  and and_1 (G0, A[0], B[0]);
  and and_2 (G1, A[1], B[1]);
  and and_3 (G2, A[2], B[2]);
  and and_4 (G3, A[3], B[3]);
  and and_5 (and_5_out, P2, P1, G0);
  and and_6 (and_6_out, P2, G1);
  and and_7 (and_7_out, P2, P1, P0, Cin);
  and and_8 (and_8_out, P3, G2);
  and and_9 (and_9_out, P3, P2, G1);
  and and_10 (and_10_out, P3, P2, P1, G0);
  and and_11 (and_11_out, P3, P2, P1, P0, Cin);
  or or_1 (Cout, G3, and_8_out, and_9_out, and_10_out, and_11_out);
  xor xor_1 (P0, A[0], B[0]);
  xor xor_2 (P1, A[1], B[1]);
  xor xor_3 (P2, A[2], B[2]);
  xor xor_4 (P3, A[3], B[3]);
  and and_12 (and_12_out, P0, Cin);
  and and_13 (and_13_out, P1, G0);
  and and_14 (and_14_out, P1, P0, Cin);
  or or_2 (C2, G2, and_6_out, and_5_out, and_7_out);
  or or_3 (C0, G0, and_12_out);
  or or_4 (C1, G1, and_13_out, and_14_out);
  ExactlyOne xor_5 (.out(Sum[0]), .in0(A[0]), .in1(B[0]), .in2(Cin));
  ExactlyOne xor_6 (.out(Sum[2]), .in0(A[2]), .in1(B[2]), .in2(C1));
  ExactlyOne xor_7 (.out(Sum[3]), .in0(A[3]), .in1(B[3]), .in2(C2));
  ExactlyOne xor_8 (.out(Sum[1]), .in0(A[1]), .in1(B[1]), .in2(C0));

  // Other names for the same wires on the sheet: C3 = Cout
endmodule

module Inputs (
  input  Halt,
  input  Clk,
  output [3:0] A,
  output [3:0] B,
  output NotDone
);

  wire A_carry, and_1_out, and_2_out, and_3_out, and_4_out, CarryB, Delay_q, nHalt;

  not not_1 (nHalt, Halt);
  and and_1 (and_1_out, nHalt, NotDone);
  Counter #(.width(4), .max('hf)) u_B (.count(and_1_out), .Q(B), .carry(CarryB), .clk(Clk));  // open: load, D, clr
  and and_2 (and_2_out, nHalt, CarryB);
  Counter #(.width(4), .max('hf), .ongoal("stay")) u_A (
    .count(and_2_out), .Q(A), .carry(A_carry), .clk(Clk));  // open: load, D, clr
  and and_3 (and_3_out, CarryB, A_carry);
  Register #(.width(1)) Delay (.D(and_3_out), .en(and_4_out), .Q(Delay_q), .clk(Clk));  // open: clr
  and and_4 (and_4_out, nHalt, NotDone);
  not not_2 (NotDone, Delay_q);
endmodule

module Checker (
  input  [3:0] A,
  input  [3:0] B,
  input  [3:0] Sum,
  input  Cout,
  output Correct,
  output [4:0] CorrectAnswer
);

  ROM #(.dataWidth(5)) rom_1 (.addr({A, B}), .data(CorrectAnswer));  // open: sel
  Comparator #(.width(5), .mode("unsigned")) comparator_1 (
    .a(CorrectAnswer), .b({Cout, Sum}), .eq(Correct));  // open: gt, lt

  // Other names for the same wires on the sheet: StudentSol[4:0] = {Cout, Sum}

  // Notes on the sheet:
  //   contents of rom_1 (hex, n*v repeats v):
  //   0 1 2 3 4 5 6 7 8 9 a b c d e f 1 2 3 4 5 6 7 8 9 a b c d e f 10 2 3 4 5 6 7 8 9 a b c d e f 10 11 3
  //   4 5 6 7 8 9 a b c d e f 10 11 12 4 5 6 7 8 9 a b c d e f 10 11 12 13 5 6 7 8 9 a b c d e f 10 11 12
  //   13 14 6 7 8 9 a b c d e f 10 11 12 13 14 15 7 8 9 a b c d e f 10 11 12 13 14 15 16 8 9 a b c d e f
  //   10 11 12 13 14 15 16 17 9 a b c d e f 10 11 12 13 14 15 16 17 18 a b c d e f 10 11 12 13 14 15 16 17
  //   18 19 b c d e f 10 11 12 13 14 15 16 17 18 19 1a c d e f 10 11 12 13 14 15 16 17 18 19 1a 1b d e f
  //   10 11 12 13 14 15 16 17 18 19 1a 1b 1c e f 10 11 12 13 14 15 16 17 18 19 1a 1b 1c 1d f 10 11 12 13
  //   14 15 16 17 18 19 1a 1b 1c 1d 1e
endmodule
