// Logisim project 4BitParity.circ as structural Verilog: 8 circuits, main circuit main
module main (
  input  Halt_Enable
);

  wire and_2_out, CLK, Correct, Done_Testing, Halt, Input, not_1_out, not_2_out, not_3_out, Solution,
       YourAnswer;
  wire [6:0] counter_1_q, TestNumber;

  not not_1 (not_1_out, Correct);
  Clock clock_1 (.out(CLK));
  and and_1 (Halt, Halt_Enable, not_1_out);
  Inputs inputs_1 (.Halt(Halt), .CLK(CLK), .Input(Input), .TestNumber(TestNumber), .Done_Testing(Done_Testing));
  _4BitEvenParity u_4bitevenparity_1 (.Input(Input), .CLK(CLK), .Is_Even(YourAnswer));
  // Probe on Input
  // Probe on YourAnswer
  // Probe on Solution
  // Probe on Correct
  not not_2 (not_2_out, Halt);
  and and_2 (and_2_out, Correct, not_2_out, not_3_out);
  not not_3 (not_3_out, Done_Testing);
  Checker checker_1 (.Your_Answer(YourAnswer), .TestNumber(TestNumber), .Correct(Correct), .Solution(Solution));
  Counter #(.width(7), .max('h41), .ongoal("stay")) counter_1 (
    .count(and_2_out), .Q(counter_1_q), .clk(CLK));  // open: load, D, carry, clr
  // Probe on counter_1_q

  // Notes on the sheet:
  //   Kun Xiao & Guoqin Sun
  //   914696908 & 914785301
  //   Max 65
endmodule

module _4BitEvenParity (
  input  Input,
  input  CLK,
  output Is_Even
);

  wire S0, S0N, S1, S1N, S2, S2N;

  D_Flip_Flop d_ff_1 (.clk(CLK), .D(S2N), .Q(S2));  // open: Qn, preset, en, reset
  D_Flip_Flop d_ff_2 (.clk(CLK), .D(S1N), .Q(S1));  // open: Qn, preset, en, reset
  D_Flip_Flop d_ff_3 (.clk(CLK), .D(S0N), .Q(S0));  // open: Qn, preset, en, reset
  S2 s2_1 (.S2(S2), .S1(S1), .S0(S0), .In(Input), .S2N(S2N));
  S1 s1_1 (.S2(S2), .S1(S1), .S0(S0), .In(Input), .S1N(S1N));
  S0 s0_1 (.S2(S2), .S1(S1), .S0(S0), .In(Input), .S0N(S0N));
  Out out_1 (.S2N(S2), .S1N(S1), .S0N(S0), .Out(Is_Even));

  // Other names for the same wires on the sheet: In = Input
endmodule

module Inputs (
  input  Halt,
  input  CLK,
  output Input,
  output [6:0] TestNumber,
  output Done_Testing
);

  wire not_1_out;

  not not_1 (not_1_out, Halt);
  Counter #(.width(7), .max('h41), .ongoal("stay")) counter_1 (
    .count(not_1_out), .Q(TestNumber), .carry(Done_Testing), .clk(CLK));  // open: load, D, clr
  ROM #(.addrWidth(7), .dataWidth(1)) rom_1 (.addr(TestNumber), .data(Input));  // open: sel

  // Notes on the sheet:
  //   contents of rom_1 (hex, n*v repeats v):
  //   7*0 1 0 0 1 0 0 0 1 1 0 1 0 0 0 1 0 1 0 1 1 0 0 4*1 0 0 0 1 0 0 1 1 0 1 0 1 0 4*1 0 0 1 1 0 4*1 0
  //   4*1
endmodule

module Checker (
  input  Your_Answer,
  input  [6:0] TestNumber,
  output Correct,
  output Solution
);

  ROM #(.addrWidth(7), .dataWidth(1)) rom_1 (.addr(TestNumber), .data(Solution));  // open: sel
  Comparator #(.width(1)) comparator_1 (.a(Solution), .b(Your_Answer), .eq(Correct));  // open: gt, lt

  // Notes on the sheet:
  //   contents of rom_1 (hex, n*v repeats v):
  //   4*0 1 11*0 1 7*0 1 0 0 0 1 11*0 1 0 0 0 1 7*0 1 11*0 1
endmodule

module S2 (
  input  S2,
  input  S1,
  input  S0,
  input  In,
  output S2N
);

  wire and_1_out, and_2_out, and_3_out, and_4_out, and_5_out, and_6_out, and_7_out, not_1_out, not_2_out,
       not_3_out, not_4_out, not_5_out, not_6_out, not_7_out, not_8_out, not_9_out, not_10_out, not_11_out,
       not_12_out;

  not not_1 (not_1_out, S2);
  not not_2 (not_2_out, S1);
  not not_3 (not_3_out, S2);
  not not_4 (not_4_out, S0);
  not not_5 (not_5_out, S1);
  not not_6 (not_6_out, S0);
  not not_7 (not_7_out, S2);
  not not_8 (not_8_out, In);
  not not_9 (not_9_out, S1);
  not not_10 (not_10_out, In);
  not not_11 (not_11_out, S0);
  not not_12 (not_12_out, In);
  and and_1 (and_1_out, not_1_out, not_2_out, In);
  and and_2 (and_2_out, not_3_out, not_4_out, In);
  and and_3 (and_3_out, not_5_out, not_6_out, In);
  and and_4 (and_4_out, not_7_out, S1, S0, not_8_out);
  and and_5 (and_5_out, S2, not_9_out, S0, not_10_out);
  and and_6 (and_6_out, S2, S1, not_11_out, not_12_out);
  and and_7 (and_7_out, S2, S1, S0, In);
  or or_1 (S2N, and_1_out, and_2_out, and_3_out, and_4_out, and_5_out, and_6_out, and_7_out);
endmodule

module S1 (
  input  S2,
  input  S1,
  input  S0,
  input  In,
  output S1N
);

  wire and_1_out, and_2_out, not_1_out, not_2_out;

  not not_1 (not_1_out, S1);
  and and_1 (and_1_out, not_1_out, S0);
  and and_2 (and_2_out, S1, not_2_out);
  not not_2 (not_2_out, S0);
  or or_1 (S1N, and_1_out, and_2_out);
endmodule

module S0 (
  input  S2,
  input  S1,
  input  S0,
  input  In,
  output S0N
);

  not not_1 (S0N, S0);
endmodule

module Out (
  input  S2N,
  input  S1N,
  input  S0N,
  output Out
);

  wire not_1_out, not_2_out;

  not not_1 (not_1_out, S1N);
  not not_2 (not_2_out, S0N);
  and and_1 (Out, S2N, not_1_out, not_2_out);
endmodule
