// Logisim project UpDownCounter.circ as structural Verilog: 7 circuits, main circuit main
module main (
  input  Halt_Enable
);

  wire and_2_out, CLK, Correct, Count_Down, Count_Up, Done_Testing, Halt, not_1_out, not_2_out, not_3_out;
  wire [2:0] Solution, Your_Answer;
  wire [5:0] counter_1_q;

  not not_1 (not_1_out, Correct);
  Clock clock_1 (.out(CLK));
  and and_1 (Halt, Halt_Enable, not_1_out);
  Inputs inputs_1 (.Halt(Halt), .CLK(CLK), .Count_Up(Count_Up), .Count_Down(Count_Down), .Done_Testing(Done_Testing));
  // Probe on Count_Up
  // Probe on Count_Down
  // Probe on Your_Answer
  // Probe on Solution
  Up_Down_Counter up_down_counter_1 (.Count_Up(Count_Up), .Count_Down(Count_Down), .CLK(CLK), .Count(Your_Answer));
  not not_2 (not_2_out, Halt);
  not not_3 (not_3_out, Done_Testing);
  Counter #(.width(6), .max('h21), .ongoal("stay")) counter_1 (
    .count(and_2_out), .Q(counter_1_q), .clk(CLK));  // open: load, D, carry, clr
  and and_2 (and_2_out, Correct, not_2_out, not_3_out);
  Checker checker_1 (
    .Halt_Enable(Halt_Enable), .Count_Up(Count_Up), .Count_Donw(Count_Down), .Your_Answer(Your_Answer),
    .CLK(CLK), .Correct(Correct), .Solution(Solution));
  // Probe on counter_1_q

  // Notes on the sheet:
  //   Your Solution in Here
  //   Kun Xiao & Guoqin Sun
  //   914696908 & 914785301
  //   Max of 33
endmodule

// S0
module Up_Down_Counter (
  input  Count_Up,
  input  Count_Down,
  input  CLK,
  output [2:0] Count
);

  wire S0N, S1N, S2N;

  S2 s2_1 (.S2(Count[2]), .S1(Count[1]), .S0(Count[0]), .Inc(Count_Up), .Dec(Count_Down), .S2N(S2N));
  S1 s1_1 (.S2(Count[2]), .S1(Count[1]), .S0(Count[0]), .Inc(Count_Up), .Dec(Count_Down), .S1N(S1N));
  S0 s0_1 (.S2(Count[2]), .S1(Count[1]), .S0(Count[0]), .Inc(Count_Up), .Dec(Count_Down), .S0N(S0N));
  D_Flip_Flop d_ff_1 (.clk(CLK), .D(S2N), .Q(Count[2]));  // open: Qn, preset, en, reset
  D_Flip_Flop d_ff_2 (.clk(CLK), .D(S1N), .Q(Count[1]));  // open: Qn, preset, en, reset
  D_Flip_Flop d_ff_3 (.clk(CLK), .D(S0N), .Q(Count[0]));  // open: Qn, preset, en, reset

  // Other names for the same wires on the sheet: S0 = Count[0]; S1 = Count[1]; S2 = Count[2]; Dec = Count_Down;
  //   Inc = Count_Up
endmodule

module Inputs (
  input  Halt,
  input  CLK,
  output Count_Up,
  output Count_Down,
  output Done_Testing
);

  wire not_1_out;
  wire [5:0] counter_1_q;

  not not_1 (not_1_out, Halt);
  Counter #(.width(6), .max('h21), .ongoal("stay")) counter_1 (
    .count(not_1_out), .Q(counter_1_q), .carry(Done_Testing), .clk(CLK));  // open: load, D, clr
  ROM #(.addrWidth(6), .dataWidth(2)) rom_1 (.addr(counter_1_q), .data({Count_Up, Count_Down}));  // open: sel

  // Notes on the sheet:
  //   contents of rom_1 (hex, n*v repeats v):
  //   0 2 0 2 0 2 0 2 0 2 0 2 0 2 0 2 0 1 0 1 0 1 0 1 0 1 0 1 0 1 0 1
endmodule

module Checker (
  input  Halt_Enable,
  input  Count_Up,
  input  Count_Donw,
  input  [2:0] Your_Answer,
  input  CLK,
  output Correct,
  output [2:0] Solution
);

  wire and_1_out, and_2_out, and_3_out, Gate, nHalt_Enable, or_2_out;

  not not_1 (nHalt_Enable, Halt_Enable);
  and and_1 (and_1_out, Correct, Halt_Enable);
  and and_2 (and_2_out, Count_Up, Gate);
  or or_1 (Gate, nHalt_Enable, and_1_out);
  and and_3 (and_3_out, Gate, Count_Donw);
  or or_2 (or_2_out, and_3_out, and_2_out);
  Counter #(.width(3), .max('h7), .ongoal("stay")) counter_1 (
    .load(and_3_out), .count(or_2_out), .Q(Solution), .clk(CLK));  // open: D, carry, clr
  Comparator #(.width(3)) comparator_1 (.a(Solution), .b(Your_Answer), .eq(Correct));  // open: gt, lt

  // Other names for the same wires on the sheet: Count_Down = Count_Donw
endmodule

module S2 (
  input  S2,
  input  S1,
  input  S0,
  input  Inc,
  input  Dec,
  output S2N
);

  wire and_1_out, and_2_out, and_3_out, and_4_out, and_5_out, not_1_out;

  not not_1 (not_1_out, Dec);
  and and_1 (and_1_out, Inc, Dec);
  and and_2 (and_2_out, S1, S0, Inc);
  and and_3 (and_3_out, S2, not_1_out);
  and and_4 (and_4_out, S2, S0);
  and and_5 (and_5_out, S2, S1);
  or or_1 (S2N, and_1_out, and_2_out, and_3_out, and_4_out, and_5_out);
endmodule

module S1 (
  input  S2,
  input  S1,
  input  S0,
  input  Inc,
  input  Dec,
  output S1N
);

  wire and_1_out, and_2_out, and_3_out, and_4_out, and_5_out, and_6_out, not_1_out, not_2_out, not_3_out,
       not_4_out, not_5_out, not_6_out;

  not not_1 (not_1_out, S1);
  not not_2 (not_2_out, S0);
  not not_3 (not_3_out, Dec);
  not not_4 (not_4_out, Inc);
  not not_5 (not_5_out, S1);
  not not_6 (not_6_out, S0);
  and and_1 (and_1_out, Inc, Dec);
  and and_2 (and_2_out, not_1_out, S0, Inc);
  and and_3 (and_3_out, S1, not_2_out, not_3_out);
  and and_4 (and_4_out, S1, S0, not_4_out);
  and and_5 (and_5_out, S2, not_5_out, not_6_out, Dec);
  and and_6 (and_6_out, S2, S1, S0);
  or or_1 (S1N, and_1_out, and_2_out, and_3_out, and_4_out, and_5_out, and_6_out);
endmodule

module S0 (
  input  S2,
  input  S1,
  input  S0,
  input  Inc,
  input  Dec,
  output S0N
);

  wire and_1_out, and_2_out, and_3_out, and_4_out, and_5_out, not_1_out, not_2_out, not_3_out, not_4_out,
       not_5_out;

  not not_1 (not_1_out, S0);
  not not_2 (not_2_out, Inc);
  not not_3 (not_3_out, Dec);
  not not_4 (not_4_out, S0);
  not not_5 (not_5_out, S0);
  and and_1 (and_1_out, not_1_out, Inc);
  and and_2 (and_2_out, S0, not_2_out, not_3_out);
  and and_3 (and_3_out, S1, not_4_out, Dec);
  and and_4 (and_4_out, S2, not_5_out, Dec);
  and and_5 (and_5_out, S2, S1, Inc);
  or or_1 (S0N, and_1_out, and_2_out, and_3_out, and_4_out, and_5_out);
endmodule
