// Logisim project Vending.circ as structural Verilog: 10 circuits, main circuit main
module main (
  input  Halt_Enable
);

  wire and_2_out, CLK, Correct, Dime, Done_Testing, Give_Dime, Give_Merch, Give_Nickel, Halt, Nickel,
       not_1_out, not_2_out, not_3_out, Quarter, Sol_Give_Dime, Sol_Give_Merch, Sol_Give_Nickel;
  wire [8:0] counter_1_q, TestNumber;

  Clock clock_1 (.out(CLK));
  not not_1 (not_1_out, Correct);
  and and_1 (Halt, Halt_Enable, not_1_out);
  Inputs inputs_1 (
    .Halt(Halt), .CLK(CLK), .Quarter(Quarter), .Dime(Dime), .Nickel(Nickel), .TestNumber(TestNumber),
    .Done_Testing(Done_Testing));
  // Probe on Quarter
  // Probe on Dime
  // Probe on Nickel
  Vending vending_1 (
    .Quarter(Quarter), .Dime(Dime), .Nickel(Nickel), .CLK(CLK), .Give_Merchandise(Give_Merch),
    .Give_Dime(Give_Dime), .Give_Nickel(Give_Nickel));
  // Probe on Correct
  // Probe on Give_Merch
  // Probe on Sol_Give_Merch
  // Probe on Give_Dime
  // Probe on Sol_Give_Dime
  // Probe on Give_Nickel
  // Probe on Sol_Give_Nickel
  not not_2 (not_2_out, Halt);
  Checker checker_1 (
    .Give_Merch(Give_Merch), .Give_Dime(Give_Dime), .Give_Nickel(Give_Nickel), .TestNumber(TestNumber),
    .Correct(Correct), .Sol_Give_Merch(Sol_Give_Merch), .Sol_Give_Dime(Sol_Give_Dime),
    .Sol_Give_Nickel(Sol_Give_Nickel));
  and and_2 (and_2_out, Correct, not_2_out, not_3_out);
  not not_3 (not_3_out, Done_Testing);
  // Probe on counter_1_q
  Counter #(.width(9), .max('h162), .ongoal("stay")) counter_1 (
    .count(and_2_out), .Q(counter_1_q), .clk(CLK));  // open: load, D, carry, clr

  // Notes on the sheet:
  //   Kun Xiao & Guoqin Sun
  //   914696908 & 914785301
  //   Max 354
endmodule

module Vending (
  input  Quarter,
  input  Dime,
  input  Nickel,
  input  CLK,
  output Give_Merchandise,
  output Give_Dime,
  output Give_Nickel
);

  wire S0, S0N, S1, S1N, S2, S2N;

  D_Flip_Flop d_ff_1 (.clk(CLK), .D(S2N), .Q(S2));  // open: Qn, preset, en, reset
  D_Flip_Flop d_ff_2 (.clk(CLK), .D(S1N), .Q(S1));  // open: Qn, preset, en, reset
  D_Flip_Flop d_ff_3 (.clk(CLK), .D(S0N), .Q(S0));  // open: Qn, preset, en, reset
  S2 s2_1 (.S2(S2), .S1(S1), .S0(S0), .Quarter(Quarter), .Dime(Dime), .Nickel(Nickel), .S2N(S2N));
  S1 s1_1 (.S2(S2), .S1(S1), .S0(S0), .Quarter(Quarter), .Dime(Dime), .Nickel(Nickel), .S1N(S1N));
  S0 s0_1 (.S2(S2), .S1(S1), .S0(S0), .Quarter(Quarter), .Dime(Dime), .Nickel(Nickel), .S0N(S0N));
  T1 t1_1 (.S2(S2), .S1(S1), .S0(S0), .Quarter(Quarter), .Dime(Dime), .Nickel(Nickel), .Quar(Give_Merchandise));
  T2 t2_1 (.S2(S2), .S1(S1), .S0(S0), .Quarter(Quarter), .Dime(Dime), .Nickel(Nickel), .Dim(Give_Dime));
  T3 t3_1 (.S2(S2), .S1(S1), .S0(S0), .Quarter(Quarter), .Dime(Dime), .Nickel(Nickel), .Quar(Give_Nickel));

  // Other names for the same wires on the sheet: Quater = Quarter
endmodule

module Inputs (
  input  Halt,
  input  CLK,
  output Quarter,
  output Dime,
  output Nickel,
  output [8:0] TestNumber,
  output Done_Testing
);

  wire not_1_out;

  not not_1 (not_1_out, Halt);
  Counter #(.width(9), .max('h162), .ongoal("stay")) counter_1 (
    .count(not_1_out), .Q(TestNumber), .carry(Done_Testing), .clk(CLK));  // open: load, D, clr
  ROM #(.addrWidth(9), .dataWidth(3)) rom_1 (.addr(TestNumber), .data({Quarter, Dime, Nickel}));  // open: sel

  // Notes on the sheet:
  //   contents of rom_1 (hex, n*v repeats v):
  //   1 0 1 0 1 0 1 0 1 0 1 0 1 0 1 0 1 0 1 0 1 0 2 0 1 0 1 0 1 0 1 0 1 0 4 0 1 0 1 0 1 0 1 0 2 0 1 0 1 0
  //   1 0 1 0 4 0 1 0 1 0 1 0 1 0 2 0 1 0 1 0 1 0 2 0 2 0 1 0 1 0 1 0 2 0 4 0 1 0 1 0 1 0 4 0 1 0 1 0 1 0
  //   1 0 2 0 1 0 1 0 1 0 2 0 2 0 1 0 1 0 1 0 2 0 4 0 1 0 1 0 2 0 2 0 1 0 1 0 2 0 4 0 1 0 1 0 4 0 1 0 1 0
  //   1 0 1 0 2 0 1 0 1 0 1 0 2 0 2 0 1 0 1 0 1 0 2 0 4 0 1 0 1 0 2 0 2 0 1 0 1 0 2 0 4 0 1 0 1 0 2 0 2 0
  //   1 0 2 0 2 0 2 0 1 0 2 0 2 0 4 0 1 0 2 0 4 0 1 0 4 0 1 0 1 0 1 0 1 0 2 0 1 0 1 0 1 0 2 0 2 0 1 0 1 0
  //   1 0 2 0 4 0 1 0 1 0 2 0 2 0 1 0 1 0 2 0 4 0 1 0 1 0 2 0 2 0 1 0 2 0 2 0 2 0 1 0 2 0 2 0 4 0 1 0 2 0
  //   4 0 1 0 1 0 2 0 2 0 1 0 2 0 2 0 2 0 1 0 2 0 2 0 4 0 2 0 2 0 2 0 2 0 2 0 4 0 2 0 4 0 1 0 4 0 2 0 4 0
  //   4 0 4
endmodule

module Checker (
  input  Give_Merch,
  input  Give_Dime,
  input  Give_Nickel,
  input  [8:0] TestNumber,
  output Correct,
  output Sol_Give_Merch,
  output Sol_Give_Dime,
  output Sol_Give_Nickel
);

  ROM #(.addrWidth(9), .dataWidth(3)) rom_1 (
    .addr(TestNumber), .data({Sol_Give_Merch, Sol_Give_Dime, Sol_Give_Nickel}));  // open: sel
  Comparator #(.width(3)) comparator_1 (
    .a({Sol_Give_Merch, Sol_Give_Dime, Sol_Give_Nickel}), .b({Give_Merch, Give_Dime, Give_Nickel}),
    .eq(Correct));  // open: gt, lt

  // Other names for the same wires on the sheet: Solution[2:0] = {Sol_Give_Merch, Sol_Give_Dime, Sol_Give_Nickel};
  //   Your_Answer[2:0] = {Give_Merch, Give_Dime, Give_Nickel}

  // Notes on the sheet:
  //   contents of rom_1 (hex, n*v repeats v):
  //   10*0 4 11*0 5 11*0 7 9*0 4 9*0 7 9*0 4 9*0 5 9*0 7 7*0 6 9*0 4 9*0 5 9*0 7 7*0 4 7*0 7 5*0 5 9*0 4
  //   9*0 5 9*0 7 7*0 4 7*0 7 7*0 4 7*0 5 7*0 7 5*0 6 0 0 0 4 9*0 4 9*0 5 9*0 7 7*0 4 7*0 7 7*0 4 7*0 5
  //   7*0 7 5*0 6 7*0 4 7*0 5 7*0 7 5*0 4 5*0 7 0 0 0 5 0 0 0 4 0 0 0 5 0 0 0 7
endmodule

module S2 (
  input  S2,
  input  S1,
  input  S0,
  input  Quarter,
  input  Dime,
  input  Nickel,
  output S2N
);

  wire and_1_out, and_2_out, and_3_out, and_4_out, and_5_out, and_6_out, not_1_out, not_2_out, not_3_out,
       not_4_out, not_5_out, not_6_out, not_7_out, not_8_out;

  not not_1 (not_1_out, S2);
  not not_2 (not_2_out, S1);
  not not_3 (not_3_out, S0);
  not not_4 (not_4_out, S0);
  not not_5 (not_5_out, Quarter);
  not not_6 (not_6_out, Dime);
  not not_7 (not_7_out, Nickel);
  not not_8 (not_8_out, S0);
  and and_1 (and_1_out, not_1_out, not_2_out, not_3_out, Quarter);
  and and_2 (and_2_out, not_4_out, Quarter, Nickel);
  and and_3 (and_3_out, S1, Dime);
  and and_4 (and_4_out, S1, S0, Nickel);
  and and_5 (and_5_out, S2, not_5_out, not_6_out, not_7_out);
  and and_6 (and_6_out, S2, not_8_out, Nickel);
  or or_1 (S2N, and_1_out, and_2_out, and_3_out, and_4_out, and_5_out, and_6_out);
endmodule

module S1 (
  input  S2,
  input  S1,
  input  S0,
  input  Quarter,
  input  Dime,
  input  Nickel,
  output S1N
);

  wire and_1_out, and_2_out, and_3_out, and_4_out, not_1_out, not_2_out, not_3_out, not_4_out, not_5_out,
       not_6_out, not_7_out, not_8_out;

  not not_1 (not_1_out, S2);
  not not_2 (not_2_out, S1);
  not not_3 (not_3_out, S2);
  not not_4 (not_4_out, S1);
  not not_5 (not_5_out, Quarter);
  not not_6 (not_6_out, Dime);
  not not_7 (not_7_out, Nickel);
  not not_8 (not_8_out, S0);
  and and_1 (and_1_out, not_1_out, not_2_out, Dime);
  and and_2 (and_2_out, not_3_out, not_4_out, S0, Nickel);
  and and_3 (and_3_out, S1, not_5_out, not_6_out, not_7_out);
  and and_4 (and_4_out, S1, not_8_out, Nickel);
  or or_1 (S1N, and_1_out, and_2_out, and_3_out, and_4_out);
endmodule

module S0 (
  input  S2,
  input  S1,
  input  S0,
  input  Quarter,
  input  Dime,
  input  Nickel,
  output S0N
);

  wire and_1_out, and_2_out, and_3_out, and_4_out, not_1_out, not_2_out, not_3_out, not_4_out, not_5_out,
       not_6_out, not_7_out, not_8_out;

  not not_1 (not_1_out, S0);
  not not_2 (not_2_out, S2);
  not not_3 (not_3_out, S1);
  not not_4 (not_4_out, S0);
  not not_5 (not_5_out, Quarter);
  not not_6 (not_6_out, Dime);
  not not_7 (not_7_out, Nickel);
  not not_8 (not_8_out, S2);
  and and_1 (and_1_out, not_1_out, Nickel);
  and and_2 (and_2_out, not_2_out, not_3_out, not_4_out, Quarter);
  and and_3 (and_3_out, S0, not_5_out, not_6_out, not_7_out);
  and and_4 (and_4_out, not_8_out, S0, Dime);
  or or_1 (S0N, and_1_out, and_2_out, and_3_out, and_4_out);
endmodule

module T1 (
  input  S2,
  input  S1,
  input  S0,
  input  Quarter,
  input  Dime,
  input  Nickel,
  output Quar
);

  wire and_1_out, and_2_out, and_3_out, and_4_out, and_5_out, not_1_out, not_2_out;

  not not_1 (not_1_out, Dime);
  not not_2 (not_2_out, Nickel);
  and and_1 (and_1_out, S0, Quarter, not_1_out, not_2_out);
  and and_2 (and_2_out, S1, Quarter);
  and and_3 (and_3_out, S2, Dime);
  and and_4 (and_4_out, S2, Quarter);
  and and_5 (and_5_out, S2, S0, Nickel);
  or or_1 (Quar, and_1_out, and_2_out, and_3_out, and_4_out, and_5_out);
endmodule

module T2 (
  input  S2,
  input  S1,
  input  S0,
  input  Quarter,
  input  Dime,
  input  Nickel,
  output Dim
);

  wire and_1_out, and_2_out;

  and and_1 (and_1_out, S1, S0, Quarter);
  and and_2 (and_2_out, S2, Quarter);
  or or_1 (Dim, and_1_out, and_2_out);
endmodule

module T3 (
  input  S2,
  input  S1,
  input  S0,
  input  Quarter,
  input  Dime,
  input  Nickel,
  output Quar
);

  wire and_1_out, and_2_out, and_3_out, not_1_out;

  not not_1 (not_1_out, S0);
  and and_1 (and_1_out, S1, not_1_out, Quarter);
  and and_2 (and_2_out, S2, Quarter);
  and and_3 (and_3_out, S2, S0, Dime);
  or or_1 (Quar, and_1_out, and_2_out, and_3_out);
endmodule
