// Logisim project CPU.circ as structural Verilog: 4 circuits, main circuit CPU
module CPU (
);

  wire CLK, Decoder, Op1, Op2, Op3, Op4, or_1_out, Reg_Write;
  wire [3:0] A, B, C, Data_In, I, R, Reg_File_b_data;
  wire [4:0] counter_1_q;

  Clock clock_1 (.out(CLK));
  or or_1 (or_1_out, Op1, Op2, Op3, Op4);
  ALU ALU (.in_1({Op4, Op3, Op2, Op1}), .in_2(R), .in_3(I), .out_4(Data_In));
  Counter #(.width(5), .max('h1f)) counter_1 (
    .count(or_1_out), .Q(counter_1_q), .clk(CLK));  // open: load, D, carry, clr
  Reg_File Reg_File (
    .A(A), .B(B), .C(C), .Data_In(Data_In), .Reg_Write(Reg_Write), .CLK(CLK), .A_DATA(R),
    .B_DATA(Reg_File_b_data));
  Multiplexer #(.width(4), .enable("false")) multiplexer_1 (.in0(Reg_File_b_data), .in1(B), .out(I), .sel(Decoder));
  ROM #(.addrWidth(5), .dataWidth(16)) rom_1 (.addr(counter_1_q), .data({Op4, Op3, Op2, Op1, C, A, B}));  // open: sel
  or or_2 (Reg_Write, Op2, Op3, Op4);
  Decoder decoder_1 (.D(Op1), .C(Op2), .B(Op3), .A(Op4), .E(Decoder));

  // Other names for the same wires on the sheet: OpCode[3:0] = {Op4, Op3, Op2, Op1}

  // Notes on the sheet:
  //   Guoqin Sun 914785301
  //   Kun Xiao 914696908
  //   Instructions
  //   contents of rom_1 (hex, n*v repeats v):
  //   2003 2106 1005 3210 4301 5433 6520 763c 8720 986f b938 ca77 db13 ec62 fd85 e05
endmodule

module Reg_File (
  input  [3:0] A,
  input  [3:0] B,
  input  [3:0] C,
  input  [3:0] Data_In,
  input  Reg_Write,
  input  CLK,
  output [3:0] A_DATA,
  output [3:0] B_DATA
);

  wire Write_Reg0, Write_Reg1, Write_Reg2, Write_Reg3, Write_Reg4, Write_Reg5, Write_Reg6, Write_Reg7,
       Write_Reg8, Write_Reg9, Write_Reg10, Write_Reg11, Write_Reg12, Write_Reg13, Write_Reg14, Write_Reg15;
  wire [3:0] Reg0, Reg1, Reg2, Reg3, Reg4, Reg5, Reg6, Reg7, Reg8, Reg9, Reg10, Reg11, Reg12, Reg13, Reg14,
       Reg15;

  Demultiplexer #(.select(4), .enable("false")) demultiplexer_1 (
    .out0(Write_Reg0), .out1(Write_Reg1), .out2(Write_Reg2), .out3(Write_Reg3), .out4(Write_Reg4),
    .out5(Write_Reg5), .out6(Write_Reg6), .out7(Write_Reg7), .out8(Write_Reg8), .out9(Write_Reg9),
    .out10(Write_Reg10), .out11(Write_Reg11), .out12(Write_Reg12), .out13(Write_Reg13), .out14(Write_Reg14),
    .out15(Write_Reg15), .in(Reg_Write), .sel(C));
  // Probe on Reg0
  Register #(.width(4)) u_Reg0 (.D(Data_In), .en(Write_Reg0), .Q(Reg0), .clk(CLK));  // open: clr
  // Probe on Reg4
  Register #(.width(4)) u_Reg4 (.D(Data_In), .en(Write_Reg4), .Q(Reg4), .clk(CLK));  // open: clr
  // Probe on Reg8
  Register #(.width(4)) u_Reg8 (.D(Data_In), .en(Write_Reg8), .Q(Reg8), .clk(CLK));  // open: clr
  // Probe on Reg12
  Register #(.width(4)) u_Reg12 (.D(Data_In), .en(Write_Reg12), .Q(Reg12), .clk(CLK));  // open: clr
  // Probe on Reg1
  Register #(.width(4)) u_Reg1 (.D(Data_In), .en(Write_Reg1), .Q(Reg1), .clk(CLK));  // open: clr
  // Probe on Reg5
  Register #(.width(4)) u_Reg5 (.D(Data_In), .en(Write_Reg5), .Q(Reg5), .clk(CLK));  // open: clr
  // Probe on Reg9
  Register #(.width(4)) u_Reg9 (.D(Data_In), .en(Write_Reg9), .Q(Reg9), .clk(CLK));  // open: clr
  // Probe on Reg13
  Register #(.width(4)) u_Reg13 (.D(Data_In), .en(Write_Reg13), .Q(Reg13), .clk(CLK));  // open: clr
  Register #(.width(4)) u_Reg2 (.D(Data_In), .en(Write_Reg2), .Q(Reg2), .clk(CLK));  // open: clr
  Register #(.width(4)) u_Reg6 (.D(Data_In), .en(Write_Reg6), .Q(Reg6), .clk(CLK));  // open: clr
  Register #(.width(4)) u_Reg10 (.D(Data_In), .en(Write_Reg10), .Q(Reg10), .clk(CLK));  // open: clr
  Register #(.width(4)) u_Reg14 (.D(Data_In), .en(Write_Reg14), .Q(Reg14), .clk(CLK));  // open: clr
  // Probe on Reg2
  // Probe on Reg6
  // Probe on Reg10
  // Probe on Reg14
  // Probe on Reg3
  Register #(.width(4)) u_Reg3 (.D(Data_In), .en(Write_Reg3), .Q(Reg3), .clk(CLK));  // open: clr
  // Probe on Reg7
  Register #(.width(4)) u_Reg7 (.D(Data_In), .en(Write_Reg7), .Q(Reg7), .clk(CLK));  // open: clr
  // Probe on Reg11
  Register #(.width(4)) u_Reg11 (.D(Data_In), .en(Write_Reg11), .Q(Reg11), .clk(CLK));  // open: clr
  // Probe on Reg15
  Register #(.width(4)) u_Reg15 (.D(Data_In), .en(Write_Reg15), .Q(Reg15), .clk(CLK));  // open: clr
  Multiplexer #(.select(4), .width(4), .enable("false")) multiplexer_1 (
    .in0(Reg0), .in1(Reg1), .in2(Reg2), .in3(Reg3), .in4(Reg4), .in5(Reg5), .in6(Reg6), .in7(Reg7),
    .in8(Reg8), .in9(Reg9), .in10(Reg10), .in11(Reg11), .in12(Reg12), .in13(Reg13), .in14(Reg14),
    .in15(Reg15), .out(A_DATA), .sel(A));
  Multiplexer #(.select(4), .width(4), .enable("false")) multiplexer_2 (
    .in0(Reg0), .in1(Reg1), .in2(Reg2), .in3(Reg3), .in4(Reg4), .in5(Reg5), .in6(Reg6), .in7(Reg7),
    .in8(Reg8), .in9(Reg9), .in10(Reg10), .in11(Reg11), .in12(Reg12), .in13(Reg13), .in14(Reg14),
    .in15(Reg15), .out(B_DATA), .sel(B));
endmodule

module ALU (
  input  [3:0] in_1,
  input  [3:0] in_2,
  input  [3:0] in_3,
  output [3:0] out_4
);

  wire [3:0] ADD, AND, NEGATE, NOT, OR, SUB, XOR;

  assign AND = in_2 & in_3;  // AND_Gate and_1, 4 bits wide
  assign OR = in_2 | in_3;  // OR_Gate or_1, 4 bits wide
  assign XOR = in_2 ^ in_3;  // XOR_Gate xor_1, 4 bits wide
  assign NOT = ~in_2;  // NOT_Gate not_1, 4 bits wide
  Negator #(.width(4)) negator_1 (.in(in_2), .out(NEGATE));
  Adder #(.width(4)) adder_1 (.a(in_2), .b(in_3), .out(ADD));  // open: cin, cout
  Subtractor #(.width(4)) subtractor_1 (.a(in_2), .b(in_3), .out(SUB));  // open: bin, bout
  Multiplexer #(.select(4), .width(4), .enable("false")) multiplexer_1 (
    .in0(4'b0000), .in1(4'b0000), .in2(in_3), .in3(in_2), .in4(AND), .in5(AND), .in6(OR), .in7(OR),
    .in8(XOR), .in9(XOR), .in10(NOT), .in11(NEGATE), .in12(ADD), .in13(ADD), .in14(SUB), .in15(SUB),
    .out(out_4), .sel(in_1));

  // Other names for the same wires on the sheet: A[3:0] = in_2; B[3:0] = in_3; Opcode[3:0] = in_1
endmodule

module Decoder (
  input  D,
  input  C,
  input  B,
  input  A,
  output E
);

  wire and_1_out, and_2_out, and_3_out, not_1_out, not_2_out, not_3_out, not_4_out;

  not not_1 (not_1_out, D);
  not not_2 (not_2_out, B);
  not not_3 (not_3_out, A);
  not not_4 (not_4_out, C);
  and and_1 (and_1_out, not_1_out, C, not_2_out, not_3_out);
  or or_1 (E, and_1_out, and_2_out, and_3_out);
  and and_2 (and_2_out, D, not_4_out, A);
  and and_3 (and_3_out, D, B);
endmodule
